# Fritzing sketch GenericHallEffect (saved by Fritzing 0.9.3b)
breadboards: 1

parts:
  VCC1 = 4 x AAA Battery Mount
  LED1 = smd LED [color="Green (555nm)" package="0805 [SMD]"]
  U2 = mystery part, 3 pins [chip_label=AH180]
  U3 = NodeMCU V1.0
  R1 = Resistor [tolerance=±5% resistance=10k package=THT]
  R2 = Resistor [tolerance=±5% resistance=1k package=THT]

nets:
  N1: VCC1.-, LED1.anode, U2.pin2, U3.GND
  N2: VCC1.+, U3.Vin
  N3: LED1.cathode, R2.Pin_0
  N4: U2.pin1, U3.3V3
  N5: U2.pin3, R1.Pin_0
  N6: U3.D3, R2.Pin_1
  N7: U3.D5, R1.Pin_1

custom parts:
  NodeMCU V1.0: ESP8266 based NodeMCU
